# Fritzing sketch combo (saved by Fritzing 0.9.10b)
breadboards: 1

parts:
  IC1 = ULN2003A [package="SO16 [SMD]"]
  Part1 = Arduino Uno (Rev3)
  S1 = Pushbutton [package="[SMD]"]
  R1 = Resistor [tolerance=±5% resistance=220 package="2512 [SMD]"]
  M1 = Stepper Motor - Unipolar
  R2 = Resistor [tolerance=±5% resistance=220 package="2512 [SMD]"]
  LED2 = smd LED [color="Red (633nm)" package="0603 [SMD]"]

nets:
  N1: IC1.In_1, Part1.D11_PWM/MOSI
  N2: IC1.In_2, Part1.D10_PWM/SS
  N3: IC1.In_3, Part1.D9_PWM
  N4: IC1.In_4, Part1.D8
  N5: IC1.0V, Part1.GND, S1.Pin_3, S1.Pin_4, R1.Pin_1, M1.C
  N6: IC1.Out_4, M1.D
  N7: IC1.Out_3, M1.COMMON_2
  N8: IC1.Out_2, M1.COMMON_1
  N9: IC1.Out_1, M1.A
  N10: Part1.D2, R2.Pin_0
  N11: Part1.D3_PWM, S1.Pin_1, S1.Pin_2, R1.Pin_0
  N12: Part1.5V, M1.B, LED2.cathode
  N13: R2.Pin_1, LED2.anode
